# Fritzing sketch esp826612Fhome (saved by Fritzing 1.0.0rc)
circuit board: 8.46667cm x 5.64444cm
breadboards: 1

parts:
  LCM1602_IIC1 = LCM1602 IIC [part_number="LCM1602 IIC" chip_label="LCM1602 IIC" package="DIP (Dual Inline) [THT]"]
  WeMos_D1_Mini1 = WeMos D1 Mini
  RHT1 = Humidity and Temperature Sensor RHT03
  R1 = Resistor [tolerance=±5% power=0.25W resistance=4.7k package=THT]
  LCD1 = LCD screen  # not connected

nets:
  N1: LCM1602_IIC1.GND, WeMos_D1_Mini1.G, RHT1.GND_2
  VCC: LCM1602_IIC1.VCC, WeMos_D1_Mini1.5V, R1.Pin_1
  N2: LCM1602_IIC1.SDA, WeMos_D1_Mini1.D2
  N3: LCM1602_IIC1.SCL, WeMos_D1_Mini1.D1
  3V3: WeMos_D1_Mini1.3V3, RHT1.Vcc
  N4: WeMos_D1_Mini1.D5, RHT1.Data-signal, R1.Pin_0

notes:
  DHT22/ AM2302
  VCC
  D5 = GPIO14
  -
  +
  SCL
  SDA
  GND
  LCD 2004

custom parts:
  LCM1602 IIC: I2C-Module to use a 1602 or 2004 LCD on with the wire.h libory Serial LCD Modul
